// Logisim project seq_circuit.circ as structural Verilog: 1 circuit, main circuit main
module main (
  input  x,
  input  y,
  output S
);

  wire adder_1_cout, d_ff_1_q;

  Adder #(.width(1)) adder_1 (.a(x), .b(y), .out(S), .cin(d_ff_1_q), .cout(adder_1_cout));
  D_Flip_Flop #(.Pre_Clr_Positions("LEGACY")) d_ff_1 (.D(adder_1_cout), .Q(d_ff_1_q));  // open: clk, Qn, preset, reset
endmodule
